// Logisim project CC4N-CPU.circ as structural Verilog: 6 circuits, main circuit main
module main (
  input  [3:0] A,
  input  [3:0] B,
  output Overflow,
  output Overflow_2,
  output [3:0] S,
  output [3:0] out_6,
  output [3:0] out_7
);

  ADD_4 add_4_1 (.in_2(B), .out_3(Overflow), .in_1(A), .out_4(out_6));
  // Probe on out_6
  Sub_4 sub_4_1 (.A(A), .Overflow(Overflow_2), .B(B), .S(out_7));
  // Probe on out_7
  Rot_Dir rot_dir_1 (.abcd(A), .xy(B[1:0]), .ABCD_2(S));
endmodule

module ADD_1 (
  input  A,
  input  B,
  input  C,
  output S,
  output Vai_1
);

  wire and_1_out, and_2_out, or_1_out, xor_1_out;

  xor xor_1 (xor_1_out, B, C);
  or or_1 (or_1_out, B, C);
  and and_1 (and_1_out, B, C);
  xor xor_2 (S, xor_1_out, A);
  and and_2 (and_2_out, or_1_out, A);
  or or_2 (Vai_1, and_2_out, and_1_out);
endmodule

module ADD_4 (
  input  [3:0] in_1,
  input  [3:0] in_2,
  output out_3,
  output [3:0] out_4
);

  wire add_1_2_vai_1, add_1_3_vai_1, add_1_4_vai_1;

  // Probe on in_2
  ADD_1 add_1_1 (.Vai_1(out_3), .A(in_2[3]), .B(in_1[3]), .C(add_1_2_vai_1), .S(out_4[3]));
  ADD_1 add_1_2 (.Vai_1(add_1_2_vai_1), .A(in_2[2]), .B(in_1[2]), .C(add_1_3_vai_1), .S(out_4[2]));
  // Probe on out_4
  // Probe on in_1
  ADD_1 add_1_3 (.Vai_1(add_1_3_vai_1), .A(in_2[1]), .B(in_1[1]), .C(add_1_4_vai_1), .S(out_4[1]));
  ADD_1 add_1_4 (.Vai_1(add_1_4_vai_1), .A(in_2[0]), .B(in_1[0]), .C(1'b0), .S(out_4[0]));
endmodule

module Sub_1 (
  input  A,
  input  B,
  input  C,
  output S,
  output Vai_1
);

  wire and_1_out, and_2_out, not_1_out, or_1_out, xor_1_out;

  xor xor_1 (xor_1_out, B, C);
  or or_1 (or_1_out, B, C);
  not not_1 (not_1_out, A);
  and and_1 (and_1_out, B, C);
  xor xor_2 (S, xor_1_out, A);
  and and_2 (and_2_out, or_1_out, not_1_out);
  or or_2 (Vai_1, and_2_out, and_1_out);
endmodule

module Sub_4 (
  input  [3:0] B,
  input  [3:0] A,
  output Overflow,
  output [3:0] S
);

  wire sub_1_2_vai_1, sub_1_3_vai_1, sub_1_4_vai_1;

  // Probe on A
  Sub_1 sub_1_1 (.Vai_1(Overflow), .A(A[3]), .B(B[3]), .C(sub_1_2_vai_1), .S(S[3]));
  Sub_1 sub_1_2 (.Vai_1(sub_1_2_vai_1), .A(A[2]), .B(B[2]), .C(sub_1_3_vai_1), .S(S[2]));
  Sub_1 sub_1_3 (.Vai_1(sub_1_3_vai_1), .A(A[1]), .B(B[1]), .C(sub_1_4_vai_1), .S(S[1]));
  // Probe on S
  Sub_1 sub_1_4 (.Vai_1(sub_1_4_vai_1), .A(A[0]), .B(B[0]), .C(1'b0), .S(S[0]));
  // Probe on B
endmodule

module Rot_Dir (
  input  [3:0] abcd,
  input  [1:0] xy,
  output [3:0] ABCD_2
);

  wire and_1_out, and_2_out, and_3_out, and_4_out, and_5_out, and_6_out, and_7_out, and_8_out, and_9_out;

  and and_1 (and_1_out, abcd[3], ~xy[1], ~xy[0]);  // AND_Gate
  and and_2 (and_2_out, abcd[2], ~xy[1], xy[0]);  // AND_Gate
  and and_3 (and_3_out, abcd[1], xy[1], ~xy[0]);  // AND_Gate
  and and_4 (and_4_out, abcd[0], xy[1], xy[0]);
  and and_5 (and_5_out, abcd[2], ~xy[1], ~xy[0]);  // AND_Gate
  and and_6 (and_6_out, abcd[1], ~xy[1], xy[0]);  // AND_Gate
  and and_7 (and_7_out, abcd[0], xy[1], ~xy[0]);  // AND_Gate
  and and_8 (and_8_out, abcd[1], ~xy[1], ~xy[0]);  // AND_Gate
  and and_9 (and_9_out, abcd[0], ~xy[1], xy[0]);  // AND_Gate
  and and_10 (ABCD_2[0], abcd[0], ~xy[1], ~xy[0]);  // AND_Gate
  or or_1 (ABCD_2[1], and_8_out, and_9_out);
  or or_2 (ABCD_2[3], and_1_out, and_2_out, and_3_out, and_4_out);
  or or_3 (ABCD_2[2], and_5_out, and_6_out, and_7_out);
endmodule
